// Logisim project 4BitParallelAdder_Subtractor.circ as structural Verilog
module _4_Bit_Parallel_Adder (
  input  A3,
  input  B3,
  input  A2,
  input  B2,
  input  A1,
  input  B1,
  input  A0,
  input  B0,
  input  C0,
  output C4,
  output S3,
  output C3,
  output S2,
  output C2,
  output S1,
  output C1,
  output S0
);

  Full_Adder full_adder_1 (.a(A3), .b(B3), .c(C3), .s(S3), .c_2(C4));
  Full_Adder full_adder_2 (.a(A2), .b(B2), .c(C2), .s(S2), .c_2(C3));
  Full_Adder full_adder_3 (.a(A1), .b(B1), .c(C1), .s(S1), .c_2(C2));
  Full_Adder full_adder_4 (.a(A0), .b(B0), .c(C0), .s(S0), .c_2(C1));
endmodule

module _4_Bit_Parallel_Subtractor (
  input  A3,
  input  B3,
  input  A2,
  input  B2,
  input  A1,
  input  B1,
  input  A0,
  input  B0,
  input  C0,
  output B4,
  output D3,
  output B3_2,
  output D2,
  output B2_2,
  output D1,
  output B1_2,
  output D0
);

  Full_Subtractor full_subtractor_1 (.in_1(A3), .in_2(B3), .in_3(B3_2), .out_4(D3), .out_5(B4));
  Full_Subtractor full_subtractor_2 (.in_1(A2), .in_2(B2), .in_3(B2_2), .out_4(D2), .out_5(B3_2));
  Full_Subtractor full_subtractor_3 (.in_1(A1), .in_2(B1), .in_3(B1_2), .out_4(D1), .out_5(B2_2));
  Full_Subtractor full_subtractor_4 (.in_1(A0), .in_2(B0), .in_3(C0), .out_4(D0), .out_5(B1_2));
endmodule
