// Logisim project Expression.circ as structural Verilog
module Expression (
  input  a,
  input  b,
  input  c,
  output y
);

  wire and_1_out, and_2_out, and_3_out, not_1_out, not_2_out, not_3_out, not_4_out, not_5_out;

  not not_1 (not_1_out, a);
  not not_2 (not_2_out, b);
  not not_3 (not_3_out, c);
  not not_4 (not_4_out, a);
  not not_5 (not_5_out, b);
  and and_1 (and_1_out, not_1_out, not_2_out, not_3_out);
  and and_2 (and_2_out, not_4_out, b, c);
  and and_3 (and_3_out, a, not_5_out, c);
  or or_1 (y, and_1_out, and_2_out, and_3_out);
endmodule
