// Logisim project HalfFull_Adder.circ as structural Verilog
module Half_Adder (
  input  a,
  input  b,
  output s,
  output c
);

  wire and_2_out, and_3_out, not_1_out, not_2_out;

  not not_1 (not_1_out, a);
  not not_2 (not_2_out, b);
  and and_1 (c, a, b);
  and and_2 (and_2_out, not_1_out, b);
  and and_3 (and_3_out, a, not_2_out);
  or or_1 (s, and_2_out, and_3_out);
endmodule

module Full_Adder (
  input  a,
  input  b,
  input  c,
  output s,
  output c_2
);

  wire nand_1_out, nand_2_out, nand_3_out, nand_4_out, nand_5_out, nand_6_out, nand_7_out;

  nand nand_1 (nand_1_out, a, b);
  nand nand_2 (nand_2_out, a, nand_1_out);
  nand nand_3 (nand_3_out, nand_1_out, b);
  nand nand_4 (nand_4_out, nand_2_out, nand_3_out);
  nand nand_5 (nand_5_out, nand_4_out, c);
  nand nand_6 (nand_6_out, nand_4_out, nand_5_out);
  nand nand_7 (nand_7_out, nand_5_out, c);
  nand nand_8 (s, nand_6_out, nand_7_out);
  nand nand_9 (c_2, nand_5_out, nand_1_out);
endmodule
