// Logisim project HalfFull_Subtractor.circ as structural Verilog
module Half_Subtractor (
  input  a,
  input  b,
  output d,
  output b2
);

  wire nand_1_out, nand_2_out, nand_3_out, nand_4_out, nand_5_out, nand_6_out;

  nand nand_1 (nand_1_out, a, a);
  nand nand_2 (nand_2_out, b, b);
  nand nand_3 (nand_3_out, a, a);
  nand nand_4 (nand_4_out, nand_1_out, b);
  nand nand_5 (nand_5_out, a, nand_2_out);
  nand nand_6 (nand_6_out, nand_3_out, b);
  nand nand_7 (d, nand_4_out, nand_5_out);
  nand nand_8 (b2, nand_6_out, nand_6_out);
endmodule

module Full_Subtractor (
  input  in_1,
  input  in_2,
  input  in_3,
  output out_4,
  output out_5
);

  wire nand_1_out, nand_2_out, nand_3_out, nand_4_out, nand_5_out, nand_6_out, nand_7_out;

  nand nand_1 (nand_1_out, in_1, in_2);
  nand nand_2 (nand_2_out, in_1, nand_1_out);
  nand nand_3 (nand_3_out, nand_1_out, in_2);
  nand nand_4 (nand_4_out, nand_2_out, nand_3_out);
  nand nand_5 (nand_5_out, nand_4_out, in_3);
  nand nand_6 (nand_6_out, nand_4_out, nand_5_out);
  nand nand_7 (nand_7_out, nand_5_out, in_3);
  nand nand_8 (out_4, nand_6_out, nand_7_out);
  nand nand_9 (out_5, nand_7_out, nand_3_out);
endmodule

module temp_fullsubtractor (
  input  a,
  input  b,
  input  c,
  output d,
  output b2
);

  wire nand_1_out, nand_2_out, nand_3_out, nand_4_out, nand_5_out, nand_6_out, nand_7_out, nand_8_out,
       nand_9_out, nand_10_out, nand_11_out, nand_12_out, nand_13_out, nand_14_out, nand_15_out, nand_16_out,
       nand_17_out, nand_18_out, nand_19_out, nand_20_out, nand_21_out, nand_22_out, nand_23_out,
       nand_25_out, nand_26_out, nand_27_out, nand_28_out;

  nand nand_1 (nand_1_out, a, a);
  nand nand_2 (nand_2_out, b, b);
  nand nand_3 (nand_3_out, a, a);
  nand nand_4 (nand_4_out, b, b);
  nand nand_5 (nand_5_out, b, c);
  nand nand_6 (nand_6_out, a, c);
  nand nand_7 (nand_7_out, nand_1_out, nand_2_out);
  nand nand_8 (nand_8_out, nand_3_out, b);
  nand nand_9 (nand_9_out, a, nand_4_out);
  nand nand_10 (nand_10_out, a, b);
  nand nand_11 (nand_11_out, nand_5_out, nand_6_out);
  nand nand_12 (nand_12_out, nand_7_out, nand_7_out);
  nand nand_13 (nand_13_out, nand_8_out, nand_8_out);
  nand nand_14 (nand_14_out, c, c);
  nand nand_15 (nand_15_out, nand_9_out, nand_9_out);
  nand nand_16 (nand_16_out, c, c);
  nand nand_17 (nand_17_out, nand_10_out, nand_10_out);
  nand nand_18 (nand_18_out, nand_11_out, nand_11_out);
  nand nand_19 (nand_19_out, a, b);
  nand nand_20 (nand_20_out, nand_12_out, c);
  nand nand_21 (nand_21_out, nand_13_out, nand_14_out);
  nand nand_22 (nand_22_out, nand_15_out, nand_16_out);
  nand nand_23 (nand_23_out, nand_17_out, c);
  nand nand_24 (b2, nand_18_out, nand_19_out);
  nand nand_25 (nand_25_out, nand_20_out, nand_21_out);
  nand nand_26 (nand_26_out, nand_22_out, nand_23_out);
  nand nand_27 (nand_27_out, nand_25_out, nand_25_out);
  nand nand_28 (nand_28_out, nand_26_out, nand_26_out);
  nand nand_29 (d, nand_27_out, nand_28_out);
endmodule
