// Logisim project ReadWriteRegisterFile.circ as structural Verilog
module _2_4_Decoder (
  input  a,
  input  b,
  output I0,
  output I1,
  output I2,
  output I3
);

  wire not_1_out, not_2_out, not_3_out, not_4_out;

  not not_1 (not_1_out, a);
  not not_2 (not_2_out, b);
  not not_3 (not_3_out, a);
  not not_4 (not_4_out, b);
  and and_1 (I3, a, b);
  and and_2 (I0, not_1_out, not_2_out);
  and and_3 (I1, not_3_out, b);
  and and_4 (I2, a, not_4_out);
endmodule

module _4_1_MUX (
  input  I0,
  input  I1,
  input  I2,
  input  I3,
  input  S0,
  input  S1,
  output Y
);

  wire and_1_out, and_2_out, and_3_out, and_4_out, not_1_out, not_2_out, not_3_out, not_4_out;

  not not_1 (not_1_out, S1);
  not not_2 (not_2_out, S0);
  not not_3 (not_3_out, S1);
  not not_4 (not_4_out, S0);
  and and_1 (and_1_out, not_1_out, not_2_out, I0);
  and and_2 (and_2_out, not_3_out, S0, I1);
  and and_3 (and_3_out, S1, not_4_out, I2);
  and and_4 (and_4_out, S1, S0, I2);
  or or_1 (Y, and_1_out, and_2_out, and_3_out, and_4_out);
endmodule

module MultiBit_MUX (
  input  [3:0] in_1,
  input  [3:0] in_2,
  input  [3:0] in_3,
  input  [3:0] in_4,
  input  S1,
  input  S0,
  output [3:0] out_7
);

  _4_1_MUX u_4_1_mux_1 (.I0(in_4[0]), .I1(in_3[0]), .I2(in_2[0]), .I3(in_1[0]), .S0(S0), .S1(S1), .Y(out_7[0]));
  _4_1_MUX u_4_1_mux_2 (.I0(in_4[1]), .I1(in_3[1]), .I2(in_2[1]), .I3(in_1[1]), .S0(S0), .S1(S1), .Y(out_7[1]));
  _4_1_MUX u_4_1_mux_3 (.I0(in_4[2]), .I1(in_3[2]), .I2(in_2[2]), .I3(in_1[2]), .S0(S0), .S1(S1), .Y(out_7[2]));
  _4_1_MUX u_4_1_mux_4 (.I0(in_4[3]), .I1(in_3[3]), .I2(in_2[3]), .I3(in_1[3]), .S0(S0), .S1(S1), .Y(out_7[3]));
endmodule

module Register (
  input  in_1,
  input  [1:0] in_2,
  input  [1:0] in_3,
  input  [1:0] in_4,
  input  [3:0] in_5,
  output [3:0] out_6,
  output [3:0] out_7
);

  wire and_1_out, and_2_out, and_3_out, and_4_out, clock_1_out, n2_4_decoder_1_i0, n2_4_decoder_1_i1,
       n2_4_decoder_1_i2, n2_4_decoder_1_i3;
  wire [3:0] register_1_q, register_2_q, register_3_q, register_4_q;

  _2_4_Decoder u_2_4_decoder_1 (
    .a(in_3[0]), .b(in_3[1]), .I0(n2_4_decoder_1_i0), .I1(n2_4_decoder_1_i1), .I2(n2_4_decoder_1_i2),
    .I3(n2_4_decoder_1_i3));
  and and_1 (and_1_out, n2_4_decoder_1_i0, in_1);
  and and_2 (and_2_out, n2_4_decoder_1_i1, in_1);
  and and_3 (and_3_out, n2_4_decoder_1_i2, in_1);
  and and_4 (and_4_out, n2_4_decoder_1_i3, in_1);
  Clock clock_1 (.out(clock_1_out));
  Register_part #(.width(4)) register_1 (.D(in_5), .en(and_1_out), .Q(register_1_q), .clk(clock_1_out));  // open: clr
  Register_part #(.width(4)) register_2 (.D(in_5), .en(and_2_out), .Q(register_2_q), .clk(clock_1_out));  // open: clr
  Register_part #(.width(4)) register_3 (.D(in_5), .en(and_3_out), .Q(register_3_q), .clk(clock_1_out));  // open: clr
  Register_part #(.width(4)) register_4 (.D(in_5), .en(and_4_out), .Q(register_4_q), .clk(clock_1_out));  // open: clr
  MultiBit_MUX multibit_mux_1 (
    .in_1(register_1_q), .in_2(register_2_q), .in_3(register_3_q), .in_4(register_4_q), .S1(in_2[1]),
    .S0(in_2[0]), .out_7(out_6));
  MultiBit_MUX multibit_mux_2 (
    .in_2(register_2_q), .in_3(register_3_q), .in_4(register_4_q), .S1(in_4[1]), .S0(in_4[0]), .out_7(out_7));  // open: in_1
endmodule
